# Fritzing sketch Fritzing_schematic (saved by Fritzing 0.9.9b)
breadboards: 2

parts:
  S1 = H-Bridge with L298N
  Part1 = Arduino Uno (Rev3) - ICSP
  Part2 = Arduino Uno (Rev3) - ICSP
  J1 = Power Jack [package=power_jack_combo]
  R1 = Rotary Potentiometer (Large) [maximum_resistance=100kΩ package=THT]
  S2 = Pushbutton [package="[THT]"]
  S3 = Pushbutton [package="[THT]"]
  R2 = Resistor [tolerance=±5% resistance=220 package="0402 [SMD]"]
  R3 = Resistor [tolerance=±5% resistance=220 package="0402 [SMD]"]
  R4 = Resistor [tolerance=±5% resistance=10k package="0402 [SMD]"]
  R5 = Resistor [tolerance=±5% resistance=10k package="0402 [SMD]"]
  LED1 = smd LED [color="Red (633nm)" package="1206 [SMD]"]
  LED2 = smd LED [color="Green (570nm)" package="1206 [SMD]"]
  J2 = Power Jack [package=power_jack_combo]
  M1 = DC Motor
  J3 = Power Jack [package=power_jack_combo]

nets:
  N1: S1.12V, J3.PWR
  GND: S1.GND, Part1.GND, Part2.GND, J1.GNDBREAK, R1.leg1, R2.Pin_1, R3.Pin_1, R4.Pin_1, R5.Pin_0, J2.GND, J2.GNDBREAK, J3.GNDBREAK
  N2: S1.ENA, Part1.D6_PWM
  N3: S1.IN1, Part1.D5_PWM
  N4: S1.IN2, Part1.D4
  N5: S1.M1-01, M1.pin_1
  N6: S1.M1-02, M1.pin_2
  N7: Part1.D8, S3.Pin_1, S3.Pin_2, R4.Pin_0
  N8: Part1.D9_PWM, S2.Pin_1, S2.Pin_2, R5.Pin_1
  N9: Part1.D0/RX, Part2.D1/TX
  N10: Part1.D1/TX, Part2.D0/RX
  N11: Part1.VIN, J1.PWR
  N12: Part2.A0, R1.wiper
  N13: Part2.D8, LED1.anode
  N14: Part2.D9_PWM, LED2.anode
  N15: Part2.5V, R1.leg2
  N16: Part2.VIN, J2.PWR
  N17: S2.Pin_3, S2.Pin_4, S3.Pin_3, S3.Pin_4
  N18: R2.Pin_0, LED1.cathode
  N19: R3.Pin_0, LED2.cathode

custom parts:
  H-Bridge with L298N: h-bridge
